// Logisim project CPU.circ as structural Verilog: 5 circuits, main circuit CPU
module CPU (
);

  wire CLK, isHALT, isIMM, not_1_out, Rwrite;
  wire [3:0] A, alu_1_result, B, C, multiplexer_1_out, OpCode, Reg_File_a_data, Reg_File_b_data;
  wire [4:0] counter_1_q;

  not not_1 (not_1_out, isHALT);
  Clock clock_1 (.out(CLK));
  Counter #(.width(5), .max('h1f)) counter_1 (
    .count(not_1_out), .Q(counter_1_q), .clk(CLK));  // open: load, D, carry, clr
  // Probe on counter_1_q
  ROM #(.addrWidth(5), .dataWidth(16)) rom_1 (.addr(counter_1_q), .data({OpCode, C, A, B}), .sel(1'b1));
  // Probe on {OpCode, C, A, B}
  // Probe on {OpCode, C, A, B}
  // Probe on A
  DEC dec_1 (.OPT_C(OpCode), .isIMM(isIMM), .reg_write(Rwrite), .isHALT(isHALT));
  Reg_File Reg_File (
    .A(A), .B(B), .C(C), .Data_In(alu_1_result), .Reg_Write(Rwrite), .CLK(CLK), .A_DATA(Reg_File_a_data),
    .B_DATA(Reg_File_b_data));
  Multiplexer #(.width(4), .enable("false")) multiplexer_1 (
    .in0(Reg_File_b_data), .in1(B), .out(multiplexer_1_out), .sel(isIMM));
  // Probe on alu_1_result
  // Probe on Reg_File_a_data
  alu alu_1 (.A_DATA(Reg_File_a_data), .B_DATA(multiplexer_1_out), .OP_code(OpCode), .RESULT(alu_1_result));

  // Notes on the sheet:
  //   Dawod Anwari, 912266152
  //   Simon Tabligan, 912676425
  //   Instructions
  //   contents of rom_1 (hex, n*v repeats v):
  //   2003 2106 1005 3210 4301 5433 6520 763c 8720 986f b938 ca77 db13 ec62 fd85 e05
endmodule

module Reg_File (
  input  [3:0] A,
  input  [3:0] B,
  input  [3:0] C,
  input  [3:0] Data_In,
  input  Reg_Write,
  input  CLK,
  output [3:0] A_DATA,
  output [3:0] B_DATA
);

  wire Write_Reg0, Write_Reg1, Write_Reg2, Write_Reg3, Write_Reg4, Write_Reg5, Write_Reg6, Write_Reg7,
       Write_Reg8, Write_Reg9, Write_Reg10, Write_Reg11, Write_Reg12, Write_Reg13, Write_Reg14, Write_Reg15;
  wire [3:0] Reg0, Reg1, Reg2, Reg3, Reg4, Reg5, Reg6, Reg7, Reg8, Reg9, Reg10, Reg11, Reg12, Reg13, Reg14,
       Reg15;

  Demultiplexer #(.select(4), .enable("false")) demultiplexer_1 (
    .out0(Write_Reg0), .out1(Write_Reg1), .out2(Write_Reg2), .out3(Write_Reg3), .out4(Write_Reg4),
    .out5(Write_Reg5), .out6(Write_Reg6), .out7(Write_Reg7), .out8(Write_Reg8), .out9(Write_Reg9),
    .out10(Write_Reg10), .out11(Write_Reg11), .out12(Write_Reg12), .out13(Write_Reg13), .out14(Write_Reg14),
    .out15(Write_Reg15), .in(Reg_Write), .sel(C));
  // Probe on Reg0
  Register #(.width(4)) u_Reg0 (.D(Data_In), .en(Write_Reg0), .Q(Reg0), .clk(CLK));  // open: clr
  // Probe on Reg4
  Register #(.width(4)) u_Reg4 (.D(Data_In), .en(Write_Reg4), .Q(Reg4), .clk(CLK));  // open: clr
  // Probe on Reg8
  Register #(.width(4)) u_Reg8 (.D(Data_In), .en(Write_Reg8), .Q(Reg8), .clk(CLK));  // open: clr
  // Probe on Reg12
  Register #(.width(4)) u_Reg12 (.D(Data_In), .en(Write_Reg12), .Q(Reg12), .clk(CLK));  // open: clr
  // Probe on Reg1
  Register #(.width(4)) u_Reg1 (.D(Data_In), .en(Write_Reg1), .Q(Reg1), .clk(CLK));  // open: clr
  // Probe on Reg5
  Register #(.width(4)) u_Reg5 (.D(Data_In), .en(Write_Reg5), .Q(Reg5), .clk(CLK));  // open: clr
  // Probe on Reg9
  Register #(.width(4)) u_Reg9 (.D(Data_In), .en(Write_Reg9), .Q(Reg9), .clk(CLK));  // open: clr
  // Probe on Reg13
  Register #(.width(4)) u_Reg13 (.D(Data_In), .en(Write_Reg13), .Q(Reg13), .clk(CLK));  // open: clr
  Register #(.width(4)) u_Reg2 (.D(Data_In), .en(Write_Reg2), .Q(Reg2), .clk(CLK));  // open: clr
  Register #(.width(4)) u_Reg6 (.D(Data_In), .en(Write_Reg6), .Q(Reg6), .clk(CLK));  // open: clr
  Register #(.width(4)) u_Reg10 (.D(Data_In), .en(Write_Reg10), .Q(Reg10), .clk(CLK));  // open: clr
  Register #(.width(4)) u_Reg14 (.D(Data_In), .en(Write_Reg14), .Q(Reg14), .clk(CLK));  // open: clr
  // Probe on Reg2
  // Probe on Reg6
  // Probe on Reg10
  // Probe on Reg14
  // Probe on Reg3
  Register #(.width(4)) u_Reg3 (.D(Data_In), .en(Write_Reg3), .Q(Reg3), .clk(CLK));  // open: clr
  // Probe on Reg7
  Register #(.width(4)) u_Reg7 (.D(Data_In), .en(Write_Reg7), .Q(Reg7), .clk(CLK));  // open: clr
  // Probe on Reg11
  Register #(.width(4)) u_Reg11 (.D(Data_In), .en(Write_Reg11), .Q(Reg11), .clk(CLK));  // open: clr
  // Probe on Reg15
  Register #(.width(4)) u_Reg15 (.D(Data_In), .en(Write_Reg15), .Q(Reg15), .clk(CLK));  // open: clr
  Multiplexer #(.select(4), .width(4), .enable("false")) multiplexer_1 (
    .in0(Reg0), .in1(Reg1), .in2(Reg2), .in3(Reg3), .in4(Reg4), .in5(Reg5), .in6(Reg6), .in7(Reg7),
    .in8(Reg8), .in9(Reg9), .in10(Reg10), .in11(Reg11), .in12(Reg12), .in13(Reg13), .in14(Reg14),
    .in15(Reg15), .out(A_DATA), .sel(A));
  Multiplexer #(.select(4), .width(4), .enable("false")) multiplexer_2 (
    .in0(Reg0), .in1(Reg1), .in2(Reg2), .in3(Reg3), .in4(Reg4), .in5(Reg5), .in6(Reg6), .in7(Reg7),
    .in8(Reg8), .in9(Reg9), .in10(Reg10), .in11(Reg11), .in12(Reg12), .in13(Reg13), .in14(Reg14),
    .in15(Reg15), .out(B_DATA), .sel(B));
endmodule

// ALU
module alu (
  input  [3:0] A_DATA,
  input  [3:0] B_DATA,
  input  [3:0] OP_code,
  output [3:0] RESULT
);

  wire [3:0] adder_1_out, adder_2_out, and_1_out, not_1_out, not_2_out, or_1_out, subtractor_1_out, xor_1_out;

  assign not_1_out = ~A_DATA;  // NOT_Gate not_1, 4 bits wide
  assign and_1_out = A_DATA & B_DATA;  // AND_Gate and_1, 4 bits wide
  assign or_1_out = A_DATA | B_DATA;  // OR_Gate or_1, 4 bits wide
  assign xor_1_out = A_DATA ^ B_DATA;  // XOR_Gate xor_1, 4 bits wide
  assign not_2_out = ~A_DATA;  // NOT_Gate not_2, 4 bits wide
  Adder #(.width(4)) adder_1 (.a(A_DATA), .b(B_DATA), .out(adder_1_out));  // open: cin, cout
  Subtractor #(.width(4)) subtractor_1 (.a(A_DATA), .b(B_DATA), .out(subtractor_1_out));  // open: bin, bout
  Adder #(.width(4)) adder_2 (.a(not_1_out), .b(4'b0001), .out(adder_2_out));  // open: cin, cout
  Multiplexer #(.select(4), .width(4), .enable("false")) multiplexer_1 (
    .in0(4'b0000), .in1(4'b0000), .in2(B_DATA), .in3(A_DATA), .in4(and_1_out), .in5(and_1_out),
    .in6(or_1_out), .in7(or_1_out), .in8(xor_1_out), .in9(xor_1_out), .in10(not_2_out), .in11(adder_2_out),
    .in12(adder_1_out), .in13(adder_1_out), .in14(subtractor_1_out), .in15(subtractor_1_out), .out(RESULT),
    .sel(OP_code));

  // Other names for the same wires on the sheet: OpCode[3:0] = OP_code
endmodule

module DEC (
  input  [3:0] OPT_C,
  output isIMM,
  output reg_write,
  output isHALT
);

  Multiplexer #(.select(4), .enable("false")) multiplexer_1 (
    .in0(1'b1), .in1(1'b1), .in2(1'b1), .in3(1'b1), .in4(OPT_C[0]), .in5(OPT_C[0]), .in6(OPT_C[0]),
    .in7(OPT_C[0]), .in8(OPT_C[0]), .in9(OPT_C[0]), .in10(OPT_C[0]), .in11(OPT_C[0]), .in12(OPT_C[0]),
    .in13(OPT_C[0]), .in14(OPT_C[0]), .in15(OPT_C[0]), .out(isIMM), .sel(OPT_C));
  Multiplexer #(.select(4), .enable("false")) multiplexer_2 (
    .in0(1'b0), .in1(1'b0), .in2(1'b1), .in3(1'b1), .in4(1'b1), .in5(1'b1), .in6(1'b1), .in7(1'b1),
    .in8(1'b1), .in9(1'b1), .in10(1'b1), .in11(1'b1), .in12(1'b1), .in13(1'b1), .in14(1'b1), .in15(1'b1),
    .out(reg_write), .sel(OPT_C));
  Multiplexer #(.select(4), .enable("false")) multiplexer_3 (
    .in0(1'b1), .in1(1'b0), .in2(1'b0), .in3(1'b0), .in4(1'b0), .in5(1'b0), .in6(1'b0), .in7(1'b0),
    .in8(1'b0), .in9(1'b0), .in10(1'b0), .in11(1'b0), .in12(1'b0), .in13(1'b0), .in14(1'b0), .in15(1'b0),
    .out(isHALT), .sel(OPT_C));
endmodule

module mem (
  input  [3:0] ALU_result,
  input  in_2,
  input  [3:0] Data_Result
);
endmodule
